# Fritzing sketch Esp8266-DeepSleep01 (saved by Fritzing 0.9.6b)
circuit board: 6.2cm x 2.9cm
breadboards: 1

parts:
  R1 = Resistor [tolerance=±5% power=0.25 resistance=470 package=THT]
  R3 = Resistor [tolerance=±5% power=0.25 resistance=100k package=THT]
  R4 = Resistor [tolerance=±5% power=0.25 resistance=10k package=THT]
  C2 = Electrolytic Capacitor [capacitance=2.2µF voltage=16V package="100 mil [THT, electrolytic]"]
  R5 = Resistor [tolerance=±5% power=0.25 resistance=1k package=THT]
  D0 = Header 1 [package=1x01_offset]
  +3_3V = Header 1 [package=1x01_offset]
  C3 = Electrolytic Capacitor [capacitance=2.2µF voltage=16V package="100 mil [THT, electrolytic]"]
  R6 = Resistor [tolerance=±5% power=0.25 resistance=470k package=THT]
  R7 = Resistor [tolerance=±5% power=0.25 resistance=10k package=THT]
  R8 = Resistor [tolerance=±5% power=0.25 resistance=33k package=THT]
  R9 = Resistor [tolerance=±5% power=0.25 resistance=1k package=THT]
  Q3 = NPN-Transistor [part_number=BC547B package="TO92 [THT]"]
  Q2 = PNP-Transistor [part_number=BC557B package="TO92 [THT]"]
  C1 = Electrolytic Capacitor [capacitance=22µF voltage=16V package="100 mil [THT, electrolytic]"]
  D1 = Diode [package=diode-1n4148]
  RST = Header 1 [package=1x01_offset]
  D2 = Header 1 [package=1x01_offset]  # not connected
  D3 = Header 1 [package=1x01_offset]  # not connected
  D4 = Header 1 [package=1x01_offset]
  D5 = Header 1 [package=1x01_offset]  # not connected
  D6 = Header 1 [package=1x01_offset]  # not connected
  D7 = Header 1 [package=1x01_offset]  # not connected
  D8 = Header 1 [package=1x01_offset]  # not connected
  5V = Header 1 [package=1x01_offset]
  A0 = Header 1 [package=1x01_offset]  # not connected
  D1_2 = Header 1 [package=1x01_offset]  # not connected
  RX = Header 1 [package=1x01_offset]  # not connected
  Q1 = PNP-Transistor [part_number=BC557B package="TO92 [THT]"]
  TX = Header 1 [package=1x01_offset]  # not connected
  JP1 = Header 3 [package=molex-1x3_lock]
  R10 = Resistor [tolerance=±5% power=0.25 resistance=4.7k package=THT]
  G = Header 1 [package=1x01_offset]
  J1 = Header 1 [package=1x01_offset]
  J2 = Header 1 [package=1x01_offset]
  +3_3V_2 = Header 1 [package=1x01_offset]
  G_2 = Header 1 [package=1x01_offset]
  G_3 = Header 1 [package=1x01_offset]
  5V_2 = Header 1 [package=1x01_offset]
  5V_3 = Header 1 [package=1x01_offset]
  G_4 = Header 1 [package=1x01_offset]
  JUMPER = Resistor [tolerance=±5% power=0.25 resistance=0 package=THT]

nets:
  N1: R1.Pin_0, D0.1
  N2: R1.Pin_1, D1.C
  N3: R3.Pin_0, Q2.E, J2.1, +3_3V_2.1, JUMPER.Pin_0
  N4: R3.Pin_1, R4.Pin_0, R6.Pin_0, C1.+, D1.A
  N5: R4.Pin_1, C2.+, Q1.B
  N6: C2.-, R5.Pin_1, C3.-, R7.Pin_1, Q3.E, C1.-, JP1.2, G.1, G_2.1, G_3.1, G_4.1
  N7: R5.Pin_0, Q1.C
  N8: +3_3V.1, JP1.3, R10.Pin_0, J1.1, JUMPER.Pin_1
  N9: C3.+, R6.Pin_1, Q2.B
  N10: R7.Pin_0, R8.Pin_0, Q2.C
  N11: R8.Pin_1, Q3.B
  N12: R9.Pin_0, RST.1, Q1.E
  N13: R9.Pin_1, Q3.C
  N14: D4.1, JP1.1, R10.Pin_1
  N15: 5V.1, 5V_2.1, 5V_3.1
